# Fritzing sketch Module_Detector (saved by Fritzing 0.9.6b)
breadboards: 1

parts:
  A1 = MQ-2 breakout
  Ultrasonic = SRF05 Ultrasonic Rangefinder
  Button_Buzzer = Pushbutton [package="[THT]"]
  LED1 = LED - 5mm [color="Red (633nm)" current=0.030 package="5 mm [THT]"]
  LED2 = LED - 5mm [color="Green (555nm)" current=0.030 package="5 mm [THT]"]
  R1 = Resistor [tolerance=±5% resistance=1k package="2010 [SMD]"]
  R2 = Resistor [tolerance=±5% resistance=1k package="2010 [SMD]"]
  M1 = DOIT Esp32 DevKit v1 (30 pins long, 11 pins width) [part_number=ESP32]
  Buzzer = Buzzer 12mm [package=buzzer-ccv-kit]

nets:
  VCC: A1.VCC, Ultrasonic.VCC, M1.3V3
  GND: A1.GND, Ultrasonic.GND, Button_Buzzer.Pin_1, Button_Buzzer.Pin_2, R2.Pin_0, M1.GND, Buzzer.2
  N1: A1.AO, M1.D4
  N2: Ultrasonic.Trig, M1.D19
  N3: Ultrasonic.Echo, M1.D18
  N4: Button_Buzzer.Pin_3, Button_Buzzer.Pin_4, M1.D5
  N5: LED1.cathode, LED2.cathode, R1.Pin_1
  N6: LED1.anode, M1.D15
  N7: LED2.anode, M1.D23
  N8: R1.Pin_0, R2.Pin_1
  N9: M1.D2, Buzzer.1

custom parts:
  MQ-2 breakout: MQ-2 gas sensor
  DOIT Esp32 DevKit v1 (30 pins long, 11 pins width): The DOIT Esp32 DevKit v1 is one of the development board created by DOIT to evaluate the ESP-WROOM-32 module. It is based on the ESP32 microcontroller that boasts Wifi, Bluetooth, Ethernet and Low Power support all in a single chip. (vanepp) made breadboard work, adjusted pin numbering and labels and reduced size of schematic and cleaned up pcb. This chip is 30pins long (2 x15) and 11 pins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
