# Fritzing sketch Modulo_Central (saved by Fritzing 0.9.6b)
breadboards: 1

parts:
  J1 = Piezo Speaker
  M1 = DOIT Esp32 DevKit v1 (30 pins long, 11 pins width) [part_number=ESP32S-PIN30]
  DHT11_1 = DHT11 module
  S1 = Momentary Switch [package=ksa_sealed_tac_switch]
  R1 = Resistor [tolerance=±5% resistance=1k power=0.25 package=THT]
  R2 = Resistor [tolerance=±5% resistance=1k power=0.25 package=THT]
  LED1 = LED - 3mm [color="Red (633nm)" current=0.030 package="3 mm [THT]"]
  LED2 = LED - 3mm [color="Green (555nm)" current=0.030 package="3 mm [THT]"]
  Display1 = LCD screen 16x2 IIC [part_number=101290]

nets:
  GND: J1.pin1, M1.GND, DHT11_1.GND, S1.1, S1.2, R1.Pin_1
  N1: J1.pin2, M1.D2
  N2: M1.3V3, DHT11_1.DATA
  N3: M1.D4, DHT11_1.VCC
  N4: M1.D5, S1.3, S1.4
  N5: M1.D18, LED1.cathode
  N6: M1.D19, LED2.cathode
  N7: M1.D21, Display1.SDA
  N8: M1.D22, Display1.SCL
  N9: R1.Pin_0, R2.Pin_1
  N10: R2.Pin_0, LED1.anode, LED2.anode

custom parts:
  DOIT Esp32 DevKit v1 (30 pins long, 11 pins width): The DOIT Esp32 DevKit v1 is one of the development board created by DOIT to evaluate the ESP-WROOM-32 module. It is based on the ESP32 microcontroller that boasts Wifi, Bluetooth, Ethernet and Low Power support all in a single chip. (vanepp) made breadboard work, adjusted pin numbering and labels and reduced size of schematic and cleaned up pcb. This chip is 30pins long (2 x15) and 11 pins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
  DHT11 module: https://cdn-learn.adafruit.com/downloads/pdf/dht.pdf DHT11 black pcb module reference by:https://github.com/adafruit/Fritzing-Library/blob/master/parts/DHT11%20Humitidy%20and%20Temperature%20Sensor.fzpz
  LCD screen 16x2 IIC: LCD screen with HD44780 controller enables showing text, symbols, value or anything else that comes from Croduino/Arduino. It is capable of showing 16 symbols in two lines and therefore can be used in many projects that need to send clearly visible and legible output information.. • Color of symbols: White • Backlight: Blue • Dimensions: 80 x 36 x 12 mm • Screen dimensions: 64.5 x 16 mm •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
